# Fritzing sketch Hookup (saved by Fritzing 0.8.3b)
breadboards: 1

parts:
  Part1 = HTU21D Breakout
  Part2 = Arduino Uno (Rev3)

nets:
  N1: Part1.SCL, Part2.A5/SCL
  N2: Part1.SDA, Part2.A4/SDA
  GND: Part1.GND, Part2.GND
  3.3V: Part1.3.3V, Part2.3V3

custom parts:
  HTU21D Breakout: This is a breadboard friendly breakout board for the Measurement Specialties high-precision, low-power digital humidity sensor.
